// Logisim project H2.circ as structural Verilog: 2 circuits, main circuit P2
module P2 (
  input  S1,
  input  S0,
  input  In,
  output S1n,
  output S0n,
  output Out
);

  wire A___0_out, A___1_out, B___0_out, B___1_out, C___0_out, D___0_out, D___1_out;

  and A___0 (A___0_out, ~S1, ~S0, ~In);  // AND_Gate
  and A___1 (A___1_out, ~S1, ~S0, In);  // AND_Gate
  and B___0 (B___0_out, ~S1, S0, ~In);  // AND_Gate
  and B___1 (B___1_out, ~S1, S0, In);  // AND_Gate
  and C___0 (C___0_out, S1, ~S0, ~In);  // AND_Gate
  and D___0 (D___0_out, S1, S0, ~In);  // AND_Gate
  and D___1 (D___1_out, In, S0, S1);
  or u_S1n (S1n, A___0_out, C___0_out, D___0_out);
  or u_S0n (S0n, A___1_out, B___1_out, C___0_out);
  or u_Out (Out, A___1_out, B___0_out, C___0_out, D___0_out, D___1_out);

  // Notes on the sheet:
  //   PROBLEM 2: IMPLEMENTING A STATE TABLE
  //   INPUT SECTION: Do not change anything here!
  //   You may only change the values of the inputs for testing using the hand tool.
  //   Do not introduce any other input or output pins in the circuit.
  //   To your logic
  //   OUTPUT SECTION: Do not change anything here!
  //   Do not introduce any other input or output pins in the circuit.
  //   From your logic
endmodule

module P3 (
  input  In,
  output Out
);

  wire A_0_out, B_0_out, B_1_out, C_0_out, D_0_out, D_1_out, E_0_out, F_0_out, F_1_out, G_0_out, G_1_out, S0,
       S0n_out, S1, S1n_out, S2, S2_p1, S2n_out;

  and A_0 (A_0_out, ~S2, ~S1, ~S0, ~In);  // AND_Gate
  and B_0 (B_0_out, ~S2, ~S1, S0, ~In);  // AND_Gate
  and B_1 (B_1_out, ~S2, ~S1, S0, In);  // AND_Gate
  and C_0 (C_0_out, ~S2, S1, ~S0, ~In);  // AND_Gate
  and D_0 (D_0_out, ~S2, S1, S0, ~In);  // AND_Gate
  and D_1 (D_1_out, ~S2, S1, S0, In);  // AND_Gate
  and E_0 (E_0_out, S2, ~S1, ~S0, ~In);  // AND_Gate
  and F_0 (F_0_out, S2, ~S1, S0, ~In);  // AND_Gate
  and F_1 (F_1_out, S2, ~S1, S0, In);  // AND_Gate
  and G_0 (G_0_out, S2, S1, ~S0, ~In);  // AND_Gate
  and G_1 (G_1_out, S2, S1, ~S0, In);  // AND_Gate
  or u_out (Out, G_0_out, G_1_out);
  or S2n (S2n_out, A_0_out, D_0_out, D_1_out, F_0_out, G_0_out, B_0_out);
  or S1n (S1n_out, D_1_out, E_0_out, F_1_out);
  or S0n (S0n_out, B_0_out, B_1_out, C_0_out, F_0_out, F_1_out);
  Clock clock_1 ();  // open: out
  // D_Flip_Flop S2: pin names not known; wires that end beside it: S2_p1, S2_p1, S2n_out, S2
  D_Flip_Flop u_S1 (.clk(S2_p1), .D(S1n_out), .Q(S1));  // open: Qn, preset, en, reset
  D_Flip_Flop u_S0 (.clk(S2_p1), .D(S0n_out), .Q(S0));  // open: Qn, preset, en, reset

  // Notes on the sheet:
  //   PROBLEM 3: IMPLEMENTING A STATE MACHINE
  //   INPUT SECTION: Do not change anything here!
  //   You may only change the values of the inputs for testing using the hand tool.
  //   Do not introduce any other input or output pins in the circuit.
  //   To your logic
  //   OUTPUT SECTION: Do not change anything here!
  //   Do not introduce any other input or output pins in the circuit.
  //   From your logic
endmodule
