// Logisim project combinational.circ as structural Verilog: 3 circuits, main circuit E3_Main
module E3_Main (
  input  A7,
  input  A6,
  input  A5,
  input  A4,
  input  A3,
  input  A2,
  input  A1,
  input  A0,
  output X7,
  output X6,
  output X5,
  output X4,
  output X3,
  output X2,
  output X1,
  output X0
);

  E3_DecrOneBit e3_decronebit_1 ();  // open: Xin, A, S, Xout
  E3_DecrOneBit e3_decronebit_2 ();  // open: Xin, A, S, Xout
  E3_DecrOneBit e3_decronebit_3 ();  // open: Xin, A, S, Xout
  E3_DecrOneBit e3_decronebit_4 ();  // open: Xin, A, S, Xout
  E3_DecrOneBit e3_decronebit_5 ();  // open: Xin, A, S, Xout
  E3_DecrOneBit e3_decronebit_6 ();  // open: Xin, A, S, Xout
  E3_DecrOneBit e3_decronebit_7 ();  // open: Xin, A, S, Xout
  E3_DecrOneBit e3_decronebit_8 ();  // open: Xin, A, S, Xout

  // Notes on the sheet:
  //   EXERCISE 3: 8-BIT DECREMENTER (Main)
  //   INPUT SECTION: Do not change anything here!
  //   You may only change the values of the inputs for testing using the hand tool.
  //   Do not introduce any other input or output pins.
  //   To your logic
  //   OUTPUT SECTION: Do not change anything here!
  //   Do not introduce any other input or output pins.
  //   From your logic
endmodule

module E3_DecrOneBit (
  input  Xin,
  input  A,
  output S,
  output Xout
);

  wire and_1_out;

  and and_1 (and_1_out, ~Xin, A);  // AND_Gate
  and and_2 (Xout, ~A, Xin);  // AND_Gate
  or or_1 (S, and_1_out, Xout);

  // Notes on the sheet:
  //   EXERCISE 3: 8-BIT DECREMENTER (DecrOneBit)
  //   INPUT SECTION: Do not change anything here!
  //   You may only change the values of the inputs for testing using the hand tool.
  //   Do not introduce any other input or output pins.
  //   To your logic
  //   OUTPUT SECTION: Do not change anything here!
  //   Do not introduce any other input or output pins.
  //   From your logic
endmodule

module E3_DecrBit0 (
  input  A,
  output S,
  output Xout
);


  // Notes on the sheet:
  //   EXERCISE 3: 8-BIT DECREMENTER (DecrBit0)
  //   INPUT SECTION: Do not change anything here!
  //   You may only change the values of the inputs for testing using the hand tool.
  //   Do not introduce any other input or output pins.
  //   To your logic
  //   OUTPUT SECTION: Do not change anything here!
  //   Do not introduce any other input or output pins.
  //   From your logic
endmodule
